# Fritzing sketch guirlande (saved by Fritzing 0.9.6b)
circuit board: 11.3216cm x 8.07268cm
breadboards: 1

parts:
  LED2' = LED - 5mm [color="Red (633nm)" current=0.030 package="5 mm [THT]"]
  LED2 = LED - 5mm [color="Red (633nm)" current=0.030 package="5 mm [THT]"]
  LED1' = LED - 5mm [color="Red (633nm)" current=0.030 package="5 mm [THT]"]
  LED3 = LED - 5mm [color="Red (633nm)" current=0.030 package="5 mm [THT]"]
  LED1 = LED - 5mm [color="Red (633nm)" current=0.030 package="5 mm [THT]"]
  R7 = Resistor [tolerance=±5% resistance=100 power=0.25 package=THT]
  R8 = Resistor [tolerance=±5% resistance=100 power=0.25 package=THT]
  R9 = Resistor [tolerance=±5% resistance=100 power=0.25 package=THT]
  LED3' = LED - 5mm [color="Red (633nm)" current=0.030 package="5 mm [THT]"]
  LED1a = LED - 5mm [color="Red (633nm)" current=0.030 package="5 mm [THT]"]
  LED3a = LED - 5mm [color="Red (633nm)" current=0.030 package="5 mm [THT]"]
  LED2a = LED - 5mm [color="Red (633nm)" current=0.030 package="5 mm [THT]"]
  LED1b = LED - 5mm [color="Red (633nm)" current=0.030 package="5 mm [THT]"]
  LED2b = LED - 5mm [color="Red (633nm)" current=0.030 package="5 mm [THT]"]
  LED3b = LED - 5mm [color="Red (633nm)" current=0.030 package="5 mm [THT]"]
  R10 = Resistor [tolerance=±5% resistance=5.4 power=0.25 package=THT]
  R11 = Resistor [tolerance=±5% resistance=5.4 power=0.25 package=THT]
  R12 = Resistor [tolerance=±5% resistance=5.4 power=0.25 package=THT]
  Q2 = npn-Powertransistor [part_number=BDW73 package="TO220 [THT]"]
  Q1 = pnp-Powertransistor [part_number=BDW74 package="TO220 [THT]"]
  Q4 = npn-Powertransistor [part_number=BDW73 package="TO220 [THT]"]
  Q6 = npn-Powertransistor [part_number=BDW73 package="TO220 [THT]"]
  Q3 = pnp-Powertransistor [part_number=BDW74 package="TO220 [THT]"]
  Q5 = pnp-Powertransistor [part_number=BDW74 package="TO220 [THT]"]
  S1 = Toggle Switch [package=THT]
  S2 = Toggle Switch [package=THT]
  S3 = Round Pushbutton
  R13 = Resistor [tolerance=±5% resistance=56k power=0.25 package=THT]
  R14 = Resistor [tolerance=±5% resistance=56k power=0.25 package=THT]
  R15 = Resistor [tolerance=±5% resistance=120k power=0.25 package=THT]
  R16 = Resistor [tolerance=±5% resistance=200k power=0.25 package=THT]
  U1 = attiny85 [package=dip]

nets:
  N1: LED2'.cathode, LED2.anode, LED1'.anode, LED1.cathode, R8.Pin_0
  N2: LED2'.anode, LED2.cathode, LED3.anode, R9.Pin_1, LED3'.cathode
  N3: LED1'.cathode, LED3.cathode, LED1.anode, R7.Pin_0, LED3'.anode
  N4: LED1a.cathode, LED2a.anode, LED1b.anode, LED2b.cathode, R10.Pin_0
  N5: LED1a.anode, LED3a.cathode, LED1b.cathode, LED3b.anode, R12.Pin_0
  N6: LED3a.anode, LED2a.cathode, LED2b.anode, LED3b.cathode, R11.Pin_0
  AA: R10.Pin_1, Q2.emitter, Q1.emitter
  BB: R11.Pin_1, Q4.emitter, Q3.emitter
  CC: R12.Pin_1, Q6.emitter, Q5.emitter
  A: Q2.base, Q1.base, U1.Pin_5
  5V: Q2.collector, Q4.collector, Q6.collector, R14.Pin_1, R15.Pin_1, R16.Pin_1, U1.Pin_8
  GND: Q1.collector, Q3.collector, Q5.collector, R13.Pin_0, U1.Pin_4
  B: Q4.base, Q3.base, U1.Pin_6
  C: Q6.base, Q5.base, U1.Pin_3
  Analog input: S1.COM, S2.COM, S3.leg1, R13.Pin_1, U1.Pin_7
  N7: S1.L2, R14.Pin_0
  N8: S2.L2, R15.Pin_0
  N9: S3.leg0, R16.Pin_0

notes:
  A'
  B'
  C'
